# Fritzing sketch ds3231 (saved by Fritzing 0.9.3b)

parts:
  Part1 = Arduino Uno (Rev3)
  ZS-042_RTC1 = ZS-042 RTC Module

nets:
  N1: Part1.A4/SDA, ZS-042_RTC1.SDA
  N2: Part1.A5/SCL, ZS-042_RTC1.SCL
  5V: Part1.5V, ZS-042_RTC1.VCC
  GND: Part1.GND, ZS-042_RTC1.GND
